# Fritzing sketch wodowskaz (saved by Fritzing 0.7.5b)
breadboards: 1

parts:
  Arduino1 = Arduino
  U1 = mystery part, 4 pins [chip_label=HC-SR04 spacing=300mil part_number=HC-SR04]
  SPKR1 = Loudspeaker

nets (from the schematic view):
  N1: Arduino1.GND, U1.pin4, SPKR1.pin1
  N2: Arduino1.D10, U1.pin3
  N3: Arduino1.D9, U1.pin2
  N4: Arduino1.D2, SPKR1.pin2
  N5: Arduino1.+5V, U1.pin1
